# Fritzing sketch ArduinoProMini33-RF-sensor-DS18B20 (saved by Fritzing 0.8.5b)
breadboards: 1

parts:
  Composants1 = Arduino Pro Mini v13
  U2 = TEMPERATURE-SENSOR [package=to-92]
  R1 = Resistor [tolerance=±5% resistance=4.7k package=THT]

nets:
  GND: Composants1.GND, U2.GND
  VCC: Composants1.VCC, U2.VCC, R1.Pin_1
  N1: Composants1.D4, U2.ADJ, R1.Pin_0
