# Fritzing sketch ArduinoProMini33-RF-sensor (saved by Fritzing 0.8.5b)
circuit board: 5.23937cm x 1.94566cm
breadboards: 1

parts:
  Composants1 = Arduino Pro Mini v13
  RFM12b1 = RFM12b HopeRF Transceiver

nets:
  N1: Composants1.DTR, Composants1.D0/TX
  N2: Composants1.GND, RFM12b1.7_GND, RFM12b1.10_GND
  N3: Composants1.VCC, RFM12b1.9_VDD
  N4: Composants1.D13/SCK, RFM12b1.13_SCK
  N5: Composants1.D12/MISO, RFM12b1.1_SDO
  N6: Composants1.D11_PWM/MOSI, RFM12b1.12_SDI
  N7: Composants1.D10_PWM/SS, RFM12b1.14_nSEL
  N8: Composants1.D2, RFM12b1.6_nRES
