# Fritzing sketch ArduinoProMini33-RF-sensor-teleinfo (saved by Fritzing 0.8.5b)
breadboards: 1

parts:
  Composants1 = Arduino Pro Mini v13
  R1 = Resistor [tolerance=±5% resistance=1.5k package=THT]
  U2 = TLP621 [package=THT]

nets:
  N1: Composants1.GND, Composants1.D2, U2.Pin_4, U2.Pin_3
  N2: R1.Pin_1, U2.Pin_1, U2.Pin_2
