# Fritzing sketch ArduinoProMini33-RF-sensor-SHT11 (saved by Fritzing 0.8.5b)
breadboards: 1

parts:
  Composants1 = Arduino Pro Mini v13
  U1 = SHT1x Humdity Sensor [package=sht1x]

nets:
  GND: Composants1.RAW, Composants1.GND, Composants1.D4, U1.GND, U1.DATA
  N1: Composants1.RESET, Composants1.A0, U1.SCK
  VCC: Composants1.VCC, U1.VDD
